// Logisim project 8_Bit_CPU.circ as structural Verilog: 1 circuit, main circuit main
module main (
  input  in_1,
  input  [7:0] in_2,
  input  in_3,
  input  in_4,
  input  in_5,
  input  in_6,
  input  in_7,
  input  in_8,
  input  in_9,
  input  in_10,
  input  in_11,
  input  in_12,
  input  in_13,
  input  in_14,
  input  in_15,
  input  in_16,
  input  in_17,
  input  in_18
);

  wire and_2_out, and_3_out, and_4_out, and_5_out, and_6_out, and_7_out, and_8_out, CLK, Four, LDADD, LDAND,
       LDBR, LDCC, LDIN1, LDIN2, LDIN3, LDIR, LDMAR, LDMDR, LDMO, LDNEXT, LDNOT, LDO1R1, LDO1R2, LDO1R3,
       LDO1ZReg, LDO2R1, LDO2R2, LDO2R3, LDO2ZReg, LDO3R1, LDO3R2, LDO3R3, LDO3ZReg, LDOR, LDPC, LDPCMAR,
       LDRW, LDST, N_q, nor_1_out, not_1_out, not_3_out, not_4_out, not_5_out, or_2_out, P_q, PCRST, Three,
       Two, undriven_2, undriven_3, Z_q;
  wire [0:0] rom_1_data_2;
  wire [3:0] rom_1_data, StateReg_q;
  wire [7:0] adder_1_out, adder_2_out, and_1_out, controlled_buffer_1_out, controlled_buffer_2_out,
       controlled_buffer_4_out, controlled_buffer_5_out, controlled_buffer_9_out, controlled_buffer_22_out,
       IR_q, MAR_q, MDR_q, not_2_out, or_1_out, PC_q, R1_q, R2_q, R3_q, ram_1_dout, undriven, ZReg_q;
  wire [7:5] IR_q_2;

  Clock clock_1 (.out(CLK));
  assign controlled_buffer_1_out = not_1_out ? controlled_buffer_4_out : 8'bz;  // Controlled_Buffer controlled_buffer_1
  not not_1 (not_1_out, Four);
  Register #(.width(4)) StateReg (.D(rom_1_data), .en(in_17), .clk(CLK), .Q(StateReg_q), .clr(in_18));
  assign controlled_buffer_2_out = LDO3R1 ? R1_q : 8'bz;  // Controlled_Buffer controlled_buffer_2
  Register R1 (.D(controlled_buffer_2_out), .en(LDIN1), .clk(CLK), .Q(R1_q), .clr(in_3));
  Register MAR (.D(controlled_buffer_2_out), .en(LDMAR), .clk(CLK), .Q(MAR_q), .clr(in_15));
  assign controlled_buffer_2_out = LDO3R2 ? R2_q : 8'bz;  // Controlled_Buffer controlled_buffer_3
  assign controlled_buffer_4_out = LDO1R1 ? R1_q : 8'bz;  // Controlled_Buffer controlled_buffer_4
  Register R2 (.D(controlled_buffer_2_out), .en(LDIN2), .clk(CLK), .Q(R2_q), .clr(in_4));
  assign controlled_buffer_5_out = LDO2R1 ? R1_q : 8'bz;  // Controlled_Buffer controlled_buffer_5
  assign controlled_buffer_4_out = LDO1R2 ? R2_q : 8'bz;  // Controlled_Buffer controlled_buffer_6
  Register R3 (.D(controlled_buffer_2_out), .en(LDIN3), .clk(CLK), .Q(R3_q), .clr(in_5));
  assign controlled_buffer_5_out = LDO2R2 ? R2_q : 8'bz;  // Controlled_Buffer controlled_buffer_7
  assign controlled_buffer_1_out = Four ? {{7{IR_q[7]}}, IR_q[0]} : 8'bz;  // Controlled_Buffer controlled_buffer_8
  assign controlled_buffer_9_out = LDST ? controlled_buffer_5_out : 8'bz;  // Controlled_Buffer controlled_buffer_9
  RAM #(.enables("line")) ram_1 (.addr(MAR_q), .we(LDRW), .clk(CLK), .din(controlled_buffer_9_out), .dout(ram_1_dout));
  assign controlled_buffer_2_out = LDO3R3 ? R3_q : 8'bz;  // Controlled_Buffer controlled_buffer_10
  assign controlled_buffer_4_out = LDO1R3 ? R3_q : 8'bz;  // Controlled_Buffer controlled_buffer_11
  assign controlled_buffer_5_out = LDO2R3 ? R3_q : 8'bz;  // Controlled_Buffer controlled_buffer_12
  assign controlled_buffer_2_out = LDADD ? adder_1_out : 8'bz;  // Controlled_Buffer controlled_buffer_13
  Adder adder_1 (.a(controlled_buffer_5_out), .b(controlled_buffer_1_out), .out(adder_1_out), .cin(in_8), .cout(in_10));
  assign controlled_buffer_2_out = LDO3ZReg ? ZReg_q : 8'bz;  // Controlled_Buffer controlled_buffer_14
  Register ZReg (.D(undriven), .en(undriven_2), .clk(undriven_3), .Q(ZReg_q), .clr(in_6));
  // NoConnect on undriven
  // NoConnect on undriven_2
  // NoConnect on undriven_3
  assign controlled_buffer_4_out = LDO1ZReg ? ZReg_q : 8'bz;  // Controlled_Buffer controlled_buffer_15
  assign controlled_buffer_5_out = LDO2ZReg ? ZReg_q : 8'bz;  // Controlled_Buffer controlled_buffer_16
  assign and_1_out = controlled_buffer_5_out & controlled_buffer_4_out;  // AND_Gate and_1, 8 bits wide
  assign or_1_out = controlled_buffer_5_out | controlled_buffer_4_out;  // OR_Gate or_1, 8 bits wide
  ROM #(.addrWidth(12), .dataWidth(36)) rom_1 (
    .addr({StateReg_q, IR_q_2, Four, Three, Two, IR_q[7], IR_q[0]}),
    .data({rom_1_data, LDO2R1, LDO2R2, LDO2R3, LDO2ZReg, LDO1R1, LDO1R2, LDO1R3, LDO1ZReg, LDADD, LDNOT, LDAND, LDOR, LDIN1, LDIN2, LDIN3, LDPC, PCRST, LDNEXT, LDBR, LDCC, LDMAR, LDRW, LDST, LDMDR, LDMO, LDIR, LDPCMAR, LDO3R1, LDO3R2, LDO3R3, LDO3ZReg, rom_1_data_2[0]}));
  assign not_2_out = ~controlled_buffer_5_out;  // NOT_Gate not_2, 8 bits wide
  assign controlled_buffer_2_out = LDAND ? and_1_out : 8'bz;  // Controlled_Buffer controlled_buffer_17
  assign controlled_buffer_2_out = LDOR ? or_1_out : 8'bz;  // Controlled_Buffer controlled_buffer_18
  Register IR (.D(MDR_q), .en(LDIR), .clk(CLK), .Q({IR_q_2, Four, Three, Two, IR_q[7], IR_q[0]}), .clr(in_14));
  Register MDR (.D(ram_1_dout), .en(LDMDR), .clk(CLK), .Q(MDR_q), .clr(in_16));
  assign controlled_buffer_2_out = LDNOT ? not_2_out : 8'bz;  // Controlled_Buffer controlled_buffer_19
  assign controlled_buffer_2_out = LDMO ? MDR_q : 8'bz;  // Controlled_Buffer controlled_buffer_20
  assign controlled_buffer_2_out = LDPCMAR ? PC_q : 8'bz;  // Controlled_Buffer controlled_buffer_21
  assign controlled_buffer_22_out = and_3_out ? controlled_buffer_4_out : 8'bz;  // Controlled_Buffer controlled_buffer_22
  and and_2 (and_2_out, controlled_buffer_2_out[7], in_9);
  and and_3 (and_3_out, LDBR, or_2_out);
  Register PC (.D(controlled_buffer_22_out), .en(LDPC), .clk(CLK), .Q(PC_q), .clr(in_7));
  assign controlled_buffer_22_out = and_4_out ? PC_q : 8'bz;  // Controlled_Buffer controlled_buffer_23
  and and_4 (and_4_out, LDBR, not_3_out);
  not not_3 (not_3_out, or_2_out);
  Register #(.width(1)) N (.D(and_2_out), .en(LDCC), .clk(CLK), .Q(N_q), .clr(in_13));
  nor nor_1 (nor_1_out, controlled_buffer_2_out[7], controlled_buffer_2_out[6], controlled_buffer_2_out[5], controlled_buffer_2_out[4], controlled_buffer_2_out[3], controlled_buffer_2_out[2], controlled_buffer_2_out[1], controlled_buffer_2_out[0]);
  and and_5 (and_5_out, Four, N_q);
  Adder adder_2 (.a(PC_q), .b(in_2), .out(adder_2_out), .cin(in_1));  // open: cout
  Register #(.width(1)) Z (.D(nor_1_out), .en(LDCC), .clk(CLK), .Q(Z_q), .clr(in_11));
  and and_6 (and_6_out, Three, Z_q);
  or or_2 (or_2_out, and_5_out, and_6_out, and_8_out);
  assign controlled_buffer_22_out = LDNEXT ? adder_2_out : 8'bz;  // Controlled_Buffer controlled_buffer_24
  not not_4 (not_4_out, nor_1_out);
  not not_5 (not_5_out, controlled_buffer_2_out[7]);
  and and_7 (and_7_out, not_4_out, not_5_out);
  Register #(.width(1)) P (.D(and_7_out), .en(LDCC), .clk(CLK), .Q(P_q), .clr(in_12));
  and and_8 (and_8_out, Two, P_q);

  // Notes on the sheet:
  //   contents of rom_1 (hex, n*v repeats v):
  //   256*100014820 256*200000100 256*300000040 16*400000000 16*500000000 32*600000000 32*700000000
  //   32*800000000 32*900000000 32*c00000000 32*e00000000 36*0 81881000 88881000 84881000 82881000
  //   41841000 48841000 44841000 42841000 21821000 28821000 24821000 22821000 4*0 81881000 88881000
  //   84881000 82881000 41841000 48841000 44841000 42841000 21821000 28821000 24821000 22821000 4*0
  //   81881000 88881000 84881000 82881000 41841000 48841000 44841000 42841000 21821000 28821000 24821000
  //   22821000 4*0 81881000 88881000 84881000 82881000 41841000 48841000 44841000 42841000 21821000
  //   28821000 24821000 22821000 4*0 81881000 88881000 84881000 82881000 41841000 48841000 44841000
  //   42841000 21821000 28821000 24821000 22821000 4*0 81881000 88881000 84881000 82881000 41841000
  //   48841000 44841000 42841000 21821000 28821000 24821000 22821000 4*0 81881000 88881000 84881000
  //   82881000 41841000 48841000 44841000 42841000 21821000 28821000 24821000 22821000 4*0 81881000
  //   88881000 84881000 82881000 41841000 48841000 44841000 42841000 21821000 28821000 24821000 22821000
  //   4*0 81881000 88881000 84881000 82881000 41841000 48841000 44841000 42841000 21821000 28821000
  //   24821000 22821000 4*0 81881000 88881000 84881000 82881000 41841000 48841000 44841000 42841000
  //   21821000 28821000 24821000 22821000 4*0 81881000 88881000 84881000 82881000 41841000 48841000
  //   44841000 42841000 21821000 28821000 24821000 22821000 4*0 81881000 88881000 84881000 82881000
  //   41841000 48841000 44841000 42841000 21821000 28821000 24821000 22821000 4*0 81881000 88881000
  //   84881000 82881000 41841000 48841000 44841000 42841000 21821000 28821000 24821000 22821000 4*0
  //   81881000 88881000 84881000 82881000 41841000 48841000 44841000 42841000 21821000 28821000 24821000
  //   22821000 4*0 81881000 88881000 84881000 82881000 41841000 48841000 44841000 42841000 21821000
  //   28821000 24821000 22821000 4*0 81881000 88881000 84881000 82881000 41841000 48841000 44841000
  //   42841000 21821000 28821000 24821000 22821000 4*0 4*80881000 4*40841000 4*20821000 4*0 4*80881000
  //   4*40841000 4*20821000 4*0 4*80881000 4*40841000 4*20821000 4*0 4*80881000 4*40841000 4*20821000 4*0
  //   4*80881000 4*40841000 4*20821000 4*0 4*80881000 4*40841000 4*20821000 4*0 4*80881000 4*40841000
  //   4*20821000 4*0 4*80881000 4*40841000 4*20821000 4*0 4*80881000 4*40841000 4*20821000 4*0 4*80881000
  //   4*40841000 4*20821000 4*0 4*80881000 4*40841000 4*20821000 4*0 4*80881000 4*40841000 4*20821000 4*0
  //   4*80881000 4*40841000 4*20821000 4*0 4*80881000 4*40841000 4*20821000 4*0 4*80881000 4*40841000
  //   4*20821000 4*0 4*80881000 4*40841000 4*20821000 4*0 4*80481000 4*40441000 4*20421000 4*0 4*80481000
  //   4*40441000 4*20421000 4*0 4*80481000 4*40441000 4*20421000 4*0 4*80481000 4*40441000 4*20421000 4*0
  //   4*80481000 4*40441000 4*20421000 4*0 4*80481000 4*40441000 4*20421000 4*0 4*80481000 4*40441000
  //   4*20421000 4*0 4*80481000 4*40441000 4*20421000 4*0 4*80481000 4*40441000 4*20421000 4*0 4*80481000
  //   4*40441000 4*20421000 4*0 4*80481000 4*40441000 4*20421000 4*0 4*80481000 4*40441000 4*20421000 4*0
  //   4*80481000 4*40441000 4*20421000 4*0 4*80481000 4*40441000 4*20421000 4*0 4*80481000 4*40441000
  //   4*20421000 4*0 4*80481000 4*40441000 4*20421000 4*0 81281000 88281000 84281000 82281000 41241000
  //   48241000 44241000 42241000 21221000 28221000 24221000 22221000 4*0 81281000 88281000 84281000
  //   82281000 41241000 48241000 44241000 42241000 21221000 28221000 24221000 22221000 4*0 81281000
  //   88281000 84281000 82281000 41241000 48241000 44241000 42241000 21221000 28221000 24221000 22221000
  //   4*0 81281000 88281000 84281000 82281000 41241000 48241000 44241000 42241000 21221000 28221000
  //   24221000 22221000 4*0 81281000 88281000 84281000 82281000 41241000 48241000 44241000 42241000
  //   21221000 28221000 24221000 22221000 4*0 81281000 88281000 84281000 82281000 41241000 48241000
  //   44241000 42241000 21221000 28221000 24221000 22221000 4*0 81281000 88281000 84281000 82281000
  //   41241000 48241000 44241000 42241000 21221000 28221000 24221000 22221000 4*0 81281000 88281000
  //   84281000 82281000 41241000 48241000 44241000 42241000 21221000 28221000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
endmodule
